# Fritzing sketch scooby (saved by Fritzing 0.9.3b)
breadboards: 1

parts:
  Componente1 = Arduino Uno (Rev3)
  DS1 = DS18B20 1-Wire Temperature Sensor [part_number=DS18B20]
  R1 = Resistor [tolerance=±5% resistance=4.7k package=THT]  # not connected
  Componente2 = HX711 Weighing Sensor Module
  Load_Cell1 = Load Cell - Red/white/black/green
  L1 = Solenoid
  D1 = Diode [package=diode-1n4001]
  Q1 = TIP120 Hi-Current Darlington Transistor
  R2 = Resistor [tolerance=±5% resistance=1k package=THT]

nets:
  N1: Componente1.D2, Componente2.CK/TX
  N2: Componente1.D3_PWM, Componente2.DO/RX
  N3: Componente1.D4, DS1.DQ
  N4: Componente1.D5_PWM, R2.Pin_1
  5V: Componente1.5V, DS1.VDD, Componente2.VCC, L1.pin2
  GND: Componente1.GND, DS1.GND, Componente2.GND, Q1.EMITTER
  N5: Componente2.E+, Load_Cell1.wire1
  N6: Componente2.E-, Load_Cell1.wire2
  N7: Componente2.A+, Load_Cell1.wire3
  N8: Componente2.A-, Load_Cell1.wire4
  N9: L1.pin1, D1.A, Q1.COLLECTOR
  N10: Q1.BASE, R2.Pin_0

custom parts:
  Load Cell - Red/white/black/green: A rectangle load cell/weighting pressure Sensor with four wires - Red, white, black, green. Normally corresponding with E+, E-, A+, A- respectively.
